# Fritzing sketch serverraumüberwachung (saved by Fritzing 1.0.1rc)
breadboards: 1

parts:
  Arduino_MEGA_2560 = Arduino Mega ADK (Rev3)
  HC-SR04_Sensor = HC-SR04 Ultrasonic Distance Sensor
  FAN = Fan - Ventilador [package=THT]
  DHT11_Sensor = DHT11 module
  16x2_LCD_Display = LCD-16X2 [package=lcd-16x2_noholes]
  LCM1602_IIC2 = LCM1602 IIC [part_number="LCM1602 IIC" chip_label="LCM1602 IIC" package="DIP (Dual Inline) [THT]"]

nets:
  N1: Arduino_MEGA_2560.D21/SCL, LCM1602_IIC2.SCL
  N2: Arduino_MEGA_2560.D20/SDA, LCM1602_IIC2.SDA
  GND: Arduino_MEGA_2560.GND, HC-SR04_Sensor.GND, FAN.GND, DHT11_Sensor.GND, LCM1602_IIC2.GND
  N3: Arduino_MEGA_2560.D9_PWM, FAN.5V
  N4: Arduino_MEGA_2560.D2_PWM, DHT11_Sensor.DATA
  N5: Arduino_MEGA_2560.D3_PWM, HC-SR04_Sensor.TRIG
  N6: Arduino_MEGA_2560.D4_PWM, HC-SR04_Sensor.ECHO
  VCC: Arduino_MEGA_2560.5V, HC-SR04_Sensor.VCC, DHT11_Sensor.VCC, LCM1602_IIC2.VCC
  VSS: 16x2_LCD_Display.VSS, LCM1602_IIC2.VSS
  VDD: 16x2_LCD_Display.VDD, LCM1602_IIC2.VDD
  N7: 16x2_LCD_Display.VO, LCM1602_IIC2.V0
  N8: 16x2_LCD_Display.RS, LCM1602_IIC2.RS
  N9: 16x2_LCD_Display.R_W, LCM1602_IIC2.RW
  N10: 16x2_LCD_Display.E, LCM1602_IIC2.E
  N11: 16x2_LCD_Display.DB0, LCM1602_IIC2.D0
  N12: 16x2_LCD_Display.DB1, LCM1602_IIC2.D1
  N13: 16x2_LCD_Display.DB2, LCM1602_IIC2.D2
  N14: 16x2_LCD_Display.DB3, LCM1602_IIC2.D3
  N15: 16x2_LCD_Display.DB4, LCM1602_IIC2.D4
  N16: 16x2_LCD_Display.DB5, LCM1602_IIC2.D5
  N17: 16x2_LCD_Display.DB6, LCM1602_IIC2.D6
  N18: 16x2_LCD_Display.DB7, LCM1602_IIC2.D7
  N19: 16x2_LCD_Display.A, LCM1602_IIC2.A
  N20: 16x2_LCD_Display.K, LCM1602_IIC2.K

custom parts:
  Fan - Ventilador: Ventilador de 2 pines, se encuentra comunmente en computadoras de escritorio
  DHT11 module: https://cdn-learn.adafruit.com/downloads/pdf/dht.pdf DHT11 black pcb module reference by:https://github.com/adafruit/Fritzing-Library/blob/master/parts/DHT11%20Humitidy%20and%20Temperature%20Sensor.fzpz
  LCM1602 IIC: I2C-Module to use a 1602 or 2004 LCD on with the wire.h libory Serial LCD Modul
